// Logisim project CIIC4082CPU_8Bit.circ as structural Verilog: 4 circuits, main circuit main
module main (
  input  [7:0] in_1,
  input  in_2,
  input  in_3,
  input  [7:0] in_4,
  input  [3:0] Ram_Test,
  input  in_6,
  input  in_7,
  input  in_8,
  input  Enable,
  input  [7:0] Input_Register,
  input  Carry_in,
  input  in_12,
  input  in_13,
  output [3:0] out_14,
  output [3:0] out_15,
  output [7:0] out_16,
  output [7:0] out_17,
  output [7:0] out_18,
  output [7:0] out_19,
  output [7:0] out_20,
  output [7:0] out_21,
  output [7:0] out_22,
  output [7:0] out_23,
  output [7:0] out_24,
  output [3:0] Counter,
  output [1:0] out_26,
  output [3:0] MARContent,
  output [2:0] out_28,
  output [7:0] MBRContent,
  output [7:0] IRContent,
  output [7:0] out_31,
  output [7:0] out_32,
  output out_33,
  output out_34,
  output out_35,
  output out_36,
  output out_37,
  output out_38,
  output out_39,
  output out_40,
  output [7:0] RegA,
  output [7:0] out_42,
  output Load,
  output Store,
  output [7:0] ALURes,
  output Carry_Out,
  output [7:0] out_47,
  output out_48,
  output out_49,
  output out_50,
  output out_51,
  output out_52,
  output out_53,
  output out_54,
  output out_55,
  output [7:0] out_56,
  output [7:0] out_57,
  output [7:0] out_58,
  output [7:0] out_59,
  output [1:0] out_60,
  output [1:0] out_61,
  output [1:0] out_62,
  output [7:0] out_63,
  output [7:0] out_64,
  output [1:0] out_65
);

  wire _2Add, _3Neg, ADDA, ADDB, Ain, ALUout, Bin, Bout, ClearSteps, Clock, CNTenable, FileIn, InternalOE,
       IRin, IRout, LOAD_t, MARin, MARout, MBRin, NEG, PCout, R0, R1, R2, R3, RAllOut, RAMld, RAMsel, STORE_t;
  wire [1:0] bitselector_3_out, bitselector_4_out, bitselector_5_out, bitselector_6_out, bitselector_7_out,
       controlled_buffer_17_out, controlled_buffer_19_out;
  wire [3:0] controlled_buffer_6_out, controlled_buffer_15_out;
  wire [7:0] controlled_buffer_9_out, InReg, IRContent_t;

  Counter #(.width(3), .max('h7)) Steps (.Q(out_28), .clk(Clock), .clr(ClearSteps));  // open: load, D, count, carry
  CU cu_1 (
    .OPC1(out_26[1]), .OPC0(out_26[0]), .SC2(out_28[2]), .SC1(out_28[1]), .SC0(out_28[0]),
    .CNTenable(CNTenable), .PCout(PCout), .MARin(MARin), .MARout(MARout), .RAMsel(RAMsel), .RAMld(RAMld),
    .MBRin(MBRin), .InternalOE(InternalOE), .IRin(IRin), .IRout(IRout), .Ain(Ain), .LOAD(LOAD_t));
  CU1 cu1_1 (
    .OPC1(out_26[1]), .OPC0(out_26[0]), .SC2(out_28[2]), .SC1(out_28[1]), .SC0(out_28[0]), .STORE(STORE_t),
    .ADDA(ADDA), .ADDB(ADDB), .NEG(NEG), .FileIn(FileIn), .RAllOut(RAllOut), .ALUout(ALUout), .Bin(Bin),
    .Bout(Bout), .ClearStep(ClearSteps));
  Clock clock_1 (.out(Clock));
  Counter #(.width(4), .max('hf)) PC (.count(CNTenable), .Q(Counter), .clk(Clock), .clr(in_8));  // open: load, D, carry
  assign out_56 = FileIn ? out_31 : 8'bz;  // Controlled_Buffer controlled_buffer_1
  Register R0_PC (.D(out_56), .en(R0), .Q(out_19), .clk(Clock), .clr(in_12));
  Register u_R1 (.D(out_56), .en(R1), .Q(out_20), .clk(Clock), .clr(in_13));
  Register u_R2 (.D(out_56), .en(R2), .Q(out_21), .clk(Clock));  // open: clr
  Register u_R3 (.D(out_56), .en(R3), .Q(out_22), .clk(Clock));  // open: clr
  Register A (.D(out_31), .en(Ain), .Q(out_23), .clk(Clock));  // open: clr
  assign InReg = R0 ? out_19 : 8'bz;  // Controlled_Buffer controlled_buffer_2
  assign InReg = R1 ? out_20 : 8'bz;  // Controlled_Buffer controlled_buffer_3
  assign InReg = R2 ? out_21 : 8'bz;  // Controlled_Buffer controlled_buffer_4
  assign InReg = R3 ? out_22 : 8'bz;  // Controlled_Buffer controlled_buffer_5
  assign controlled_buffer_6_out = PCout ? Counter : 4'bz;  // Controlled_Buffer controlled_buffer_6
  ALU ALU (
    .Input_Register(InReg), .Add(_2Add), .Carry_in(Carry_in), .Input_A(out_23), .Carry_out(Carry_Out),
    ._2_s(_3Neg), .Add_out(ALURes), ._2_s_Out(ALURes));
  assign out_31 = RAllOut ? InReg : 8'bz;  // Controlled_Buffer controlled_buffer_7
  assign out_31 = ALUout ? ALURes : 8'bz;  // Controlled_Buffer controlled_buffer_8
  Register B (.D(out_31), .en(Bin), .Q(out_24), .clk(Clock));  // open: clr
  BitSelector #(.group(4)) bitselector_1 (.in(controlled_buffer_9_out), .out(controlled_buffer_6_out), .sel(1'b0));
  Register IR (.D(out_31), .en(IRin), .Q(IRContent), .clk(Clock));  // open: clr
  assign controlled_buffer_9_out = IRout ? IRContent : 8'bz;  // Controlled_Buffer controlled_buffer_9
  assign out_31 = Bout ? out_24 : 8'bz;  // Controlled_Buffer controlled_buffer_10
  assign IRContent_t = 1'b1 ? IRContent : 8'bz;  // Controlled_Buffer controlled_buffer_11
  BitSelector #(.group(2)) bitselector_2 (.in(IRContent_t), .out(out_26), .sel(2'b11));
  assign out_31 = in_2 ? in_1 : 8'bz;  // Controlled_Buffer controlled_buffer_12
  Decoder #(.select(2)) decoder_1 (.out0(Load), .out1(Store), .out2(_2Add), .out3(_3Neg), .sel(out_26), .en(1'b1));
  BitSelector #(.group(2)) bitselector_3 (.in(IRContent_t), .out(bitselector_3_out), .sel(2'b10));
  assign out_65 = _3Neg ? bitselector_3_out : 2'bz;  // Controlled_Buffer controlled_buffer_13
  Decoder #(.select(2)) decoder_2 (.out0(R0), .out1(R1), .out2(R2), .out3(R3), .sel(out_65), .en(NEG));
  Register #(.width(4)) MAR (.D(controlled_buffer_6_out), .en(MARin), .Q(MARContent), .clk(Clock));  // open: clr
  assign out_31 = InternalOE ? MBRContent : 8'bz;  // Controlled_Buffer controlled_buffer_14
  Register MBR (.D(out_31), .en(MBRin), .Q(MBRContent), .clk(Clock));  // open: clr
  assign controlled_buffer_15_out = MARout ? MARContent : 4'bz;  // Controlled_Buffer controlled_buffer_15
  assign out_31 = Enable ? MBRContent : 8'bz;  // Controlled_Buffer controlled_buffer_16
  Decoder #(.select(2)) decoder_3 (
    .out0(R0), .out1(R1), .out2(R2), .out3(R3), .sel(controlled_buffer_17_out), .en(LOAD_t));
  BitSelector #(.group(2)) bitselector_4 (.in(IRContent_t), .out(bitselector_4_out), .sel(2'b10));
  assign controlled_buffer_17_out = Load ? bitselector_4_out : 2'bz;  // Controlled_Buffer controlled_buffer_17
  assign controlled_buffer_15_out = in_3 ? Ram_Test : 4'bz;  // Controlled_Buffer controlled_buffer_18
  BitSelector #(.group(2)) bitselector_5 (.in(IRContent_t), .out(bitselector_5_out), .sel(2'b10));
  assign controlled_buffer_19_out = Store ? bitselector_5_out : 2'bz;  // Controlled_Buffer controlled_buffer_19
  Decoder #(.select(2)) decoder_4 (
    .out0(R0), .out1(R1), .out2(R2), .out3(R3), .sel(controlled_buffer_19_out), .en(STORE_t));
  assign out_31 = in_7 ? in_4 : 8'bz;  // Controlled_Buffer controlled_buffer_20
  RAM #(.addrWidth(4), .bus("asynch")) ram_1 (
    .addr(controlled_buffer_15_out), .data(out_31), .sel(RAMsel), .ld(RAMld), .clr(in_6));
  BitSelector #(.group(2)) bitselector_6 (.in(IRContent_t), .out(bitselector_6_out), .sel(2'b10));
  assign out_61 = _2Add ? bitselector_6_out : 2'bz;  // Controlled_Buffer controlled_buffer_21
  Decoder #(.select(2)) decoder_5 (.out0(R0), .out1(R1), .out2(R2), .out3(R3), .sel(out_61), .en(ADDA));
  BitSelector #(.group(2)) bitselector_7 (.in(IRContent_t), .out(bitselector_7_out), .sel(2'b01));
  assign out_60 = _2Add ? bitselector_7_out : 2'bz;  // Controlled_Buffer controlled_buffer_22
  Decoder #(.select(2)) decoder_6 (.out0(R0), .out1(R1), .out2(R2), .out3(R3), .sel(out_60), .en(ADDB));

  assign out_14 = Counter;
  assign out_15 = MARContent;
  assign out_16 = MBRContent;
  assign out_17 = IRContent;
  assign out_18 = ALURes;
  assign out_32 = out_31;
  assign out_33 = out_31[7];
  assign out_34 = out_31[6];
  assign out_35 = out_31[5];
  assign out_36 = out_31[4];
  assign out_37 = out_31[3];
  assign out_38 = out_31[2];
  assign out_39 = out_31[1];
  assign out_40 = out_31[0];
  assign out_42 = out_31;
  assign out_47 = out_24;
  assign out_48 = out_31[7];
  assign out_49 = out_31[6];
  assign out_50 = out_31[5];
  assign out_51 = out_31[4];
  assign out_52 = out_31[3];
  assign out_53 = out_31[2];
  assign out_54 = out_31[1];
  assign out_55 = out_31[0];
  assign out_57 = out_31;
  assign out_58 = out_19;
  assign out_59 = out_20;
  assign out_62 = out_26;
  assign out_63 = out_21;
  assign out_64 = out_22;
  assign RegA = out_23;

  // Other names for the same wires on the sheet: _0Load = Load; _1Store = Store; ALU[7:0] = ALURes; B[7:0] = out_24;
  //   A[7:0] = out_23; InA[7:0] = out_23; IR[7:0] = IRContent; MAR[3:0] = MARContent; MBR[7:0] = MBRContent;
  //   OPC[1:0] = out_26; PC[3:0] = Counter; Reg0[7:0] = out_19; Reg1[7:0] = out_20; Reg2[7:0] = out_21;
  //   Reg3[7:0] = out_22

  // Notes on the sheet:
  //   Control Unit
  //   PCout
  //   Internal Address Bus 4 Bits
  //   8 bit number divided on groups of 2
  //   00 10 11 01 g3 g2 g1 g0
  //   MARin
  //   Internal Address Bus 8 Bits
  //   Neg
  //   Load
  //   External Address Bus 4 Bits
  //   Store
  //   External Address Bus 8 Bits
  //   Add A
  //   Add B
endmodule

module ALU (
  input  [7:0] Input_Register,
  input  Add,
  input  Carry_in,
  input  [7:0] Input_A,
  input  _2_s,
  output [7:0] Add_out,
  output Carry_out,
  output [7:0] _2_s_Out
);

  wire [7:0] _2_s_Buffer_out, Add_Buffer_out;

  assign Add_Buffer_out = Add ? Input_Register : 8'bz;  // Controlled_Buffer Add_Buffer
  assign _2_s_Buffer_out = _2_s ? Input_Register : 8'bz;  // Controlled_Buffer _2_s_Buffer
  Negator negator_1 (.in(_2_s_Buffer_out), .out(_2_s_Out));
  Adder adder_1 (.a(Add_Buffer_out), .b(Input_A), .out(Add_out), .cin(Carry_in), .cout(Carry_out));
endmodule

module CU (
  input  OPC1,
  input  OPC0,
  input  SC2,
  input  SC1,
  input  SC0,
  output CNTenable,
  output PCout,
  output MARin,
  output MARout,
  output RAMsel,
  output RAMld,
  output MBRin,
  output InternalOE,
  output IRin,
  output IRout,
  output Ain,
  output LOAD
);

  wire and_1_out, and_2_out, and_3_out, and_4_out, and_5_out, and_6_out, and_7_out, and_8_out, and_9_out,
       and_10_out, and_11_out, and_12_out, and_13_out, and_14_out, and_15_out, and_16_out, and_17_out,
       and_18_out, and_19_out, and_20_out, and_22_out, and_23_out, not_1_out, not_2_out, not_3_out,
       not_4_out, not_5_out, not_6_out, not_7_out, not_8_out, not_9_out, not_10_out, not_11_out, not_12_out,
       not_13_out, not_14_out, not_15_out, not_16_out, not_17_out, not_18_out, not_19_out, not_20_out,
       not_21_out, not_22_out, not_23_out, not_24_out, not_25_out, not_26_out, not_27_out, not_28_out,
       not_29_out, not_30_out, not_31_out, not_32_out, not_33_out, not_34_out, not_35_out, not_36_out,
       not_37_out, not_38_out, not_39_out, not_40_out, not_41_out, not_42_out, not_43_out, not_44_out,
       not_45_out, not_46_out, not_47_out, not_48_out, not_49_out, not_50_out, not_51_out, not_52_out,
       not_53_out, not_54_out, not_55_out, not_56_out, not_57_out, not_58_out, not_59_out, not_60_out,
       not_61_out;

  not not_1 (not_1_out, OPC0);
  not not_2 (not_2_out, SC0);
  not not_3 (not_3_out, OPC1);
  not not_4 (not_4_out, SC1);
  not not_5 (not_5_out, SC1);
  not not_6 (not_6_out, SC0);
  not not_7 (not_7_out, SC2);
  not not_8 (not_8_out, SC1);
  not not_9 (not_9_out, SC0);
  not not_10 (not_10_out, OPC0);
  not not_11 (not_11_out, SC1);
  not not_12 (not_12_out, SC0);
  not not_13 (not_13_out, SC2);
  not not_14 (not_14_out, SC1);
  not not_15 (not_15_out, SC0);
  not not_16 (not_16_out, OPC1);
  not not_17 (not_17_out, OPC0);
  not not_18 (not_18_out, OPC1);
  not not_19 (not_19_out, SC2);
  not not_20 (not_20_out, OPC0);
  not not_21 (not_21_out, SC1);
  not not_22 (not_22_out, SC0);
  not not_23 (not_23_out, SC2);
  not not_24 (not_24_out, SC1);
  not not_25 (not_25_out, OPC1);
  not not_26 (not_26_out, SC1);
  not not_27 (not_27_out, SC0);
  not not_28 (not_28_out, SC2);
  not not_29 (not_29_out, SC1);
  not not_30 (not_30_out, OPC1);
  not not_31 (not_31_out, SC1);
  not not_32 (not_32_out, SC0);
  not not_33 (not_33_out, SC2);
  not not_34 (not_34_out, SC1);
  not not_35 (not_35_out, SC2);
  not not_36 (not_36_out, SC0);
  not not_37 (not_37_out, OPC1);
  not not_38 (not_38_out, OPC0);
  not not_39 (not_39_out, SC1);
  not not_40 (not_40_out, SC2);
  not not_41 (not_41_out, SC1);
  not not_42 (not_42_out, OPC1);
  not not_43 (not_43_out, OPC0);
  not not_44 (not_44_out, SC1);
  not not_45 (not_45_out, SC0);
  not not_46 (not_46_out, SC2);
  not not_47 (not_47_out, SC0);
  not not_48 (not_48_out, OPC1);
  not not_49 (not_49_out, OPC0);
  not not_50 (not_50_out, SC1);
  not not_51 (not_51_out, SC2);
  not not_52 (not_52_out, SC0);
  not not_53 (not_53_out, OPC1);
  not not_54 (not_54_out, OPC0);
  not not_55 (not_55_out, OPC1);
  not not_56 (not_56_out, SC2);
  not not_57 (not_57_out, OPC0);
  not not_58 (not_58_out, SC2);
  not not_59 (not_59_out, OPC1);
  not not_60 (not_60_out, OPC0);
  not not_61 (not_61_out, SC1);
  and and_1 (and_1_out, not_1_out, SC2, SC1, not_2_out);
  and and_2 (and_2_out, not_3_out, OPC0, SC2, not_4_out, SC0);
  and and_3 (and_3_out, OPC1, OPC0, SC2, not_5_out, not_6_out);
  and and_4 (and_4_out, not_7_out, not_8_out, not_9_out);
  and and_5 (and_5_out, OPC1, not_10_out, not_11_out, not_12_out);
  and and_6 (and_6_out, not_13_out, not_14_out, not_15_out);
  and and_7 (and_7_out, not_16_out, not_17_out, SC1, SC0);
  and and_8 (and_8_out, not_18_out, not_19_out, SC1, SC0);
  and and_9 (and_9_out, OPC1, not_20_out, not_21_out, not_22_out);
  and and_10 (and_10_out, not_23_out, not_24_out, SC0);
  and and_11 (and_11_out, not_25_out, SC2, not_26_out, not_27_out);
  and and_12 (and_12_out, not_28_out, not_29_out, SC0);
  and and_13 (and_13_out, not_30_out, SC2, not_31_out, not_32_out);
  and and_14 (and_14_out, not_33_out, not_34_out, SC0);
  and and_15 (and_15_out, not_35_out, SC1, not_36_out);
  and and_16 (and_16_out, not_37_out, not_38_out, SC2, not_39_out);
  and and_17 (and_17_out, not_40_out, not_41_out, SC0);
  and and_18 (and_18_out, not_42_out, not_43_out, SC2, not_44_out, not_45_out);
  and and_19 (and_19_out, not_46_out, SC1, not_47_out);
  and and_20 (and_20_out, not_48_out, not_49_out, SC2, not_50_out, SC0);
  and and_21 (IRin, not_51_out, SC1, not_52_out);
  and and_22 (and_22_out, not_53_out, not_54_out, SC1, SC0);
  and and_23 (and_23_out, not_55_out, not_56_out, SC1, SC0);
  and and_24 (Ain, OPC1, not_57_out, not_58_out, SC1, SC0);
  and and_25 (LOAD, not_59_out, not_60_out, SC2, not_61_out, SC0);
  or or_1 (CNTenable, and_1_out, and_2_out, and_3_out);
  or or_2 (PCout, and_4_out, and_5_out);
  or or_3 (MARin, and_6_out, and_7_out, and_8_out, and_9_out);
  or or_4 (MARout, and_10_out, and_11_out);
  or or_5 (RAMsel, and_12_out, and_13_out);
  or or_6 (RAMld, and_14_out, and_15_out, and_16_out);
  or or_7 (MBRin, and_17_out, and_18_out);
  or or_8 (InternalOE, and_19_out, and_20_out);
  or or_9 (IRout, and_22_out, and_23_out);
endmodule

module CU1 (
  input  OPC1,
  input  OPC0,
  input  SC2,
  input  SC1,
  input  SC0,
  output STORE,
  output ADDA,
  output ADDB,
  output NEG,
  output FileIn,
  output RAllOut,
  output ALUout,
  output Bin,
  output Bout,
  output ClearStep
);

  wire and_2_out, and_3_out, and_6_out, and_7_out, and_8_out, and_9_out, and_10_out, and_11_out, not_1_out,
       not_2_out, not_3_out, not_4_out, not_5_out, not_6_out, not_7_out, not_8_out, not_9_out, not_10_out,
       not_11_out, not_12_out, not_13_out, not_14_out, not_15_out, not_16_out, not_17_out, not_18_out,
       not_19_out, not_20_out, not_21_out, not_22_out, not_23_out, not_24_out, not_25_out, not_26_out,
       not_27_out, not_28_out, not_29_out, not_30_out;

  not not_1 (not_1_out, OPC1);
  not not_2 (not_2_out, SC1);
  not not_3 (not_3_out, SC0);
  not not_4 (not_4_out, OPC0);
  not not_5 (not_5_out, SC2);
  not not_6 (not_6_out, OPC0);
  not not_7 (not_7_out, SC1);
  not not_8 (not_8_out, OPC0);
  not not_9 (not_9_out, SC1);
  not not_10 (not_10_out, SC0);
  not not_11 (not_11_out, SC2);
  not not_12 (not_12_out, OPC0);
  not not_13 (not_13_out, SC1);
  not not_14 (not_14_out, SC2);
  not not_15 (not_15_out, OPC1);
  not not_16 (not_16_out, SC1);
  not not_17 (not_17_out, SC0);
  not not_18 (not_18_out, OPC0);
  not not_19 (not_19_out, SC2);
  not not_20 (not_20_out, OPC0);
  not not_21 (not_21_out, SC1);
  not not_22 (not_22_out, SC0);
  not not_23 (not_23_out, SC2);
  not not_24 (not_24_out, OPC0);
  not not_25 (not_25_out, SC1);
  not not_26 (not_26_out, SC0);
  not not_27 (not_27_out, OPC0);
  not not_28 (not_28_out, SC1);
  not not_29 (not_29_out, OPC1);
  not not_30 (not_30_out, SC0);
  and and_1 (STORE, not_1_out, OPC0, SC2, not_2_out, not_3_out);
  and and_2 (and_2_out, OPC1, not_4_out, not_5_out, SC1, SC0);
  and and_3 (and_3_out, OPC1, not_6_out, SC2, not_7_out, SC0);
  and and_4 (ADDB, OPC1, not_8_out, SC2, not_9_out, not_10_out);
  and and_5 (NEG, OPC1, OPC0, not_11_out, SC1, SC0);
  and and_6 (and_6_out, not_12_out, SC2, not_13_out, SC0);
  and and_7 (and_7_out, OPC1, OPC0, not_14_out, SC1, SC0);
  and and_8 (and_8_out, not_15_out, OPC0, SC2, not_16_out, not_17_out);
  and and_9 (and_9_out, OPC1, not_18_out, not_19_out, SC1, SC0);
  and and_10 (and_10_out, OPC1, not_20_out, SC2, not_21_out, not_22_out);
  and and_11 (and_11_out, OPC1, OPC0, not_23_out, SC1, SC0);
  and and_12 (Bin, OPC1, not_24_out, SC2, not_25_out, not_26_out);
  and and_13 (Bout, OPC1, not_27_out, SC2, not_28_out, SC0);
  and and_14 (ClearStep, not_29_out, OPC0, SC2, SC1, not_30_out);
  or or_1 (ADDA, and_2_out, and_3_out);
  or or_2 (FileIn, and_6_out, and_7_out);
  or or_3 (RAllOut, and_8_out, and_9_out);
  or or_4 (ALUout, and_10_out, and_11_out);
endmodule
